# Fritzing sketch Mixer (saved by Fritzing 0.9.2b)
breadboards: 1

parts:
  R1 = Resistor [tolerance=±5% resistance=10k package=THT]
  R2 = Rotary Potentiometer (Small) [maximum_resistance=10kΩ package=THT]
  C1 = Electrolytic Capacitor [capacitance=1µF package="100 mil [THT, electrolytic]"]
  JP1 = RCA [package=rca_lock]
  U1 = LM 358 Dual Op-Amp [package="DIP8 [THT]"]
  R3 = Resistor [tolerance=±5% resistance=10k package=THT]
  C2 = Ceramic Capacitor [capacitance=100nF package="100 mil [THT, multilayer]"]
  R4 = Resistor [tolerance=±5% resistance=10 package=THT]
  R5 = Resistor [tolerance=±5% resistance=10k package=THT]
  C3 = Ceramic Capacitor [capacitance=1pF package="100 mil [THT, multilayer]"]

nets:
  N1: R1.Pin_0, C1.-
  N2: R1.Pin_1, U1.connector1, R3.Pin_0, C2.0
  GND: R2.leg1, JP1.SHELL, U1.connector2, U1.connector3, U1.connector4
  N3: R2.wiper, C1.+
  N4: R2.leg2, JP1.PIN
  N5: U1.connector0, R3.Pin_1, C2.1, R4.Pin_0
  N6: U1.connector5, R4.Pin_1, R5.Pin_0, C3.0
  N7: U1.connector6, R5.Pin_1, C3.1
